# Fritzing sketch LoopinBoard (saved by Fritzing 0.9.2b)
circuit board: 1.34261cm x 2.15458cm
perfboards: 1

parts:
  M1 = DC Motor
  LM = Voltage Regulator [part_number="7805 (5V regulator)" package=to220-igo]
  VCC1 = Battery block 9V
  S1 = SPST Switch [package=switch-spdt]
  Q1 = TRANSISTOR_NPN [part_number="Power Mosfet" package=to-92-ammo]
  Attiny = attiny85 [part_number=Attiny package=dip]
  R1 = Resistor [tolerance=±5% resistance=10k package=THT]

nets:
  N1: M1.pin_1, LM.IN, S1.S
  N2: M1.pin_2, Q1.C
  N3: LM.GND, VCC1.-, Q1.E, Attiny.Pin_4
  N4: LM.OUT, Attiny.Pin_8
  N5: VCC1.+, S1.P
  N6: Q1.B, R1.Pin_1
  N7: Attiny.Pin_5, R1.Pin_0

notes:
  <- MOSFET
